# Fritzing sketch First Day Example (saved by Fritzing 0.9.3b)
breadboards: 1

parts:
  BAT1 = Battery Holders [package=lipo-1100mAh]
  LED1 = LED - 3mm [color="Red (633nm)" package="3 mm [THT]"]
  R1 = Resistor [tolerance=±5% resistance=220 package=THT]

nets:
  N1: BAT1.+, R1.Pin_0
  N2: BAT1.-, LED1.cathode
  N3: LED1.anode, R1.Pin_1
